# Fritzing sketch electronic_sketch (saved by Fritzing 1.0.4)
breadboards: 1

parts:
  Composant1 = Arduino Uno (Rev3) - ICSP
  M1 = Dagu DGServo 9g (Pan and tilt) [part_number=RS001B]
  M2 = Dagu DGServo 9g (Pan and tilt) [part_number=RS001B]
  LCD1 = LCD screen  # not connected
  IC1 = SELECTOR_MULTIPLEXER [package=so016]  # not connected
  M3 = RioRand LM2596
  Composant2 = InvenSense MPU6050  # not connected
  ESP32_-_Back2 = ESP32 - CAM
  ESP32_-_Back3 = ESP32 - CAM
  M4 = Stepper Motor - Bipolar
  M5 = Stepper Motor - Bipolar
  M6 = Stepper Motor - Bipolar
  RE1 = Rotary Encoder [package=THT]  # not connected
  Arduino_CNC_Shield_V3_00_1 = Arduino_CNC_V3.00
  M7 = Dagu DGServo 9g (Pan and tilt) [part_number=RS001B]
  M8 = Dagu DGServo 9g (Pan and tilt) [part_number=RS001B]
  Power_plug1 = Power plug
  Power_plug2 = Power plug
  J1 = Basic Servo
  M9 = >Wemos D1 R32  # not connected
  JL012-13-5_1 = JL012-13-5.2 Lever (Limit) Switch SPDT + NO + NC [part_number=JL012-13-5.2]
  JL012-13-5_2 = JL012-13-5.2 Lever (Limit) Switch SPDT + NO + NC [part_number=JL012-13-5.2]

nets:
  N1: Composant1.GND, ESP32_-_Back3.GND#16, JL012-13-5_1.C
  N2: Composant1.D4, JL012-13-5_1.NO
  N3: Composant1.D6_PWM, ESP32_-_Back3.GPIO4
  N4: Composant1.D7, JL012-13-5_2.NO
  GND: M1.gnd, M2.gnd, M3.Pin_4, ESP32_-_Back2.GND, ESP32_-_Back3.GND#7, M7.gnd, M8.gnd, J1.gnd
  VCC: M1.vcc, M2.vcc, M3.Pin_3, ESP32_-_Back2.5V, M8.vcc
  N5: M1.pulse, ESP32_-_Back3.GPIO14
  N6: M2.pulse, ESP32_-_Back3.GPIO15
  N7: M3.Pin_1, Power_plug2.VCC
  N8: M3.Pin_2, Power_plug2.GND
  N9: ESP32_-_Back3.GPIO2, M8.pulse
  N10: ESP32_-_Back3.GPIO13, M7.pulse
  N11: ESP32_-_Back3.GPIO12, J1.pulse
  VCC_2: ESP32_-_Back3.5V, M7.vcc, J1.vcc
  N12: M4.A, Arduino_CNC_Shield_V3_00_1.Y-MTR_'4'
  N13: M4.C, Arduino_CNC_Shield_V3_00_1.Y-MTR_'3'
  N14: M4.B, Arduino_CNC_Shield_V3_00_1.Y-MTR_'2'
  N15: M4.D, Arduino_CNC_Shield_V3_00_1.Y-MTR_'1'
  N16: M5.A, Arduino_CNC_Shield_V3_00_1.Z-MTR_'4'
  N17: M5.C, Arduino_CNC_Shield_V3_00_1.Z-MTR_'3'
  N18: M5.B, Arduino_CNC_Shield_V3_00_1.Z-MTR_'2'
  N19: M5.D, Arduino_CNC_Shield_V3_00_1.Z-MTR_'1'
  N20: M6.A, Arduino_CNC_Shield_V3_00_1.X-MTR_'4'
  N21: M6.C, Arduino_CNC_Shield_V3_00_1.X-MTR_'3'
  N22: M6.B, Arduino_CNC_Shield_V3_00_1.X-MTR_'2'
  N23: M6.D, Arduino_CNC_Shield_V3_00_1.X-MTR_'1'
  N24: Arduino_CNC_Shield_V3_00_1.POWER_-, Power_plug1.GND
  N25: Arduino_CNC_Shield_V3_00_1.POWER_+, Power_plug1.VCC

custom parts:
  ESP32 - CAM: The ESP32-CAM has a very competitive small-size camera module that can operate independently as a minimum system with a footprint of only 27*40.5*4.5mm and a deep sleep current of up to 6mA.
  Arduino_CNC_V3.00: Protoneer Arduino CNC Shield V3.00 If using Grbl V0.9: The “A” axis can not be used (yet). The “SCL” (Arduino A5) pin is now used for 'Probing' input. The “End Stops Z+ & Z-” (Arduino D11) and “SpnEn” (Arduino D12) have been switched!
  >Wemos D1 R32: Wemos D1 R32 - This board is used with dual-mode Wi-Fi and Bluetooth chips, which is safe, reliable, and scalable to a variety of applications. DC in 5V-12V, 1 analog input(3.2V max input), a Micro USB connection, Compatible with D1 R32=WiFi+bluetooth+UNO
  JL012-13-5.2 Lever (Limit) Switch SPDT + NO + NC: Micro Switch; Model No.: JL012-13.5-2; Actuator Action: Momentary; Actuator Type: Hinge Lever; Contact Configuration: 1NO, 1NC (SPDT) Temperature -25~65℃；Relative humidity: below 85%; Rate Voltage: 125V AC; Rated Current: 1A.
