# Fritzing sketch newest_electronic_sketch_lcd_wemos (saved by Fritzing 1.0.4)
breadboards: 1

parts:
  Composant1 = Arduino Uno (Rev3) - ICSP  # not connected
  LCD1 = LCD screen
  IC1 = SELECTOR_MULTIPLEXER [package=so016]  # not connected
  M3 = RioRand LM2596
  Composant2 = InvenSense MPU6050  # not connected
  M5 = Stepper Motor - Bipolar
  RE1 = Rotary Encoder [package=THT]  # not connected
  Arduino_CNC_Shield_V3_00_1 = Arduino_CNC_V3.00
  Power_plug2 = Power plug
  JL012-13-5_1 = JL012-13-5.2 Lever (Limit) Switch SPDT + NO + NC [part_number=JL012-13-5.2]
  JL012-13-5_2 = JL012-13-5.2 Lever (Limit) Switch SPDT + NO + NC [part_number=JL012-13-5.2]
  J1 = Basic Servo
  M8 = Dagu DGServo 9g (Top view) [part_number=RS001B]
  M9 = Dagu DGServo 9g (Top view) [part_number=RS001B]
  M10 = >Wemos D1 R32  # not connected
  Composant3 = Arduino Uno (Rev3) - ICSP

nets:
  GND: LCD1.VSS, LCD1.LED-, M3.Pin_4, J1.gnd, M8.gnd, M9.gnd, Composant3.GND
  VDD: LCD1.VDD, Composant3.3V3
  N1: LCD1.RS, Composant3.D13/SCK
  N2: LCD1.E, Composant3.D12/MISO
  N3: LCD1.DB4, Composant3.D5_PWM
  N4: LCD1.DB5, Composant3.D4
  N5: LCD1.DB6, Composant3.D3_PWM
  N6: LCD1.DB7, Composant3.D2
  N7: LCD1.LED+, Composant3.5V
  N8: M3.Pin_1, Power_plug2.VCC
  N9: M3.Pin_2, Power_plug2.GND
  VCC: M3.Pin_3, J1.vcc, M9.vcc, Composant3.VIN
  N10: M5.A, Arduino_CNC_Shield_V3_00_1.Z-MTR_'4'
  N11: M5.C, Arduino_CNC_Shield_V3_00_1.Z-MTR_'3'
  N12: M5.B, Arduino_CNC_Shield_V3_00_1.Z-MTR_'2'
  N13: M5.D, Arduino_CNC_Shield_V3_00_1.Z-MTR_'1'
  N14: Arduino_CNC_Shield_V3_00_1.RX, Composant3.D0/RX
  N15: Arduino_CNC_Shield_V3_00_1.TX, Composant3.D1/TX
  N16: Arduino_CNC_Shield_V3_00_1.SpnEn_/_Z_Limit, JL012-13-5_1.C
  N17: Arduino_CNC_Shield_V3_00_1.SpnEn_(Gnd), JL012-13-5_1.NC
  N18: Arduino_CNC_Shield_V3_00_1.SpnDir, JL012-13-5_2.C
  N19: Arduino_CNC_Shield_V3_00_1.SpnDir_(Gnd), JL012-13-5_2.NC
  N20: J1.pulse, Composant3.D11_PWM/MOSI
  N21: M8.pulse, Composant3.D10_PWM/SS
  N22: M9.pulse, Composant3.D9_PWM

custom parts:
  Arduino_CNC_V3.00: Protoneer Arduino CNC Shield V3.00 If using Grbl V0.9: The “A” axis can not be used (yet). The “SCL” (Arduino A5) pin is now used for 'Probing' input. The “End Stops Z+ & Z-” (Arduino D11) and “SpnEn” (Arduino D12) have been switched!
  JL012-13-5.2 Lever (Limit) Switch SPDT + NO + NC: Micro Switch; Model No.: JL012-13.5-2; Actuator Action: Momentary; Actuator Type: Hinge Lever; Contact Configuration: 1NO, 1NC (SPDT) Temperature -25~65℃；Relative humidity: below 85%; Rate Voltage: 125V AC; Rated Current: 1A.
  >Wemos D1 R32: Wemos D1 R32 - This board is used with dual-mode Wi-Fi and Bluetooth chips, which is safe, reliable, and scalable to a variety of applications. DC in 5V-12V, 1 analog input(3.2V max input), a Micro USB connection, Compatible with D1 R32=WiFi+bluetooth+UNO
