# Fritzing sketch electronic_sketch (saved by Fritzing 1.0.4)
breadboards: 1

parts:
  Composant1 = Arduino Uno (Rev3) - ICSP
  M1 = Dagu DGServo 9g (Pan and tilt) [part_number=RS001B]
  M2 = Dagu DGServo 9g (Pan and tilt) [part_number=RS001B]
  LCD1 = LCD screen  # not connected
  IC1 = SELECTOR_MULTIPLEXER [package=so016]  # not connected
  M3 = RioRand LM2596
  Composant2 = InvenSense MPU6050  # not connected
  ESP32_-_Back2 = ESP32 - CAM
  ESP32_-_Back3 = ESP32 - CAM
  M4 = Stepper Motor - Bipolar
  M5 = Stepper Motor - Bipolar
  M6 = Stepper Motor - Bipolar
  RE1 = Rotary Encoder [package=THT]  # not connected
  Arduino_CNC_Shield_V3_00_1 = Arduino_CNC_V3.00
  M7 = Dagu DGServo 9g (Pan and tilt) [part_number=RS001B]
  M8 = Dagu DGServo 9g (Pan and tilt) [part_number=RS001B]
  Power_plug1 = Power plug
  Power_plug2 = Power plug
  S2 = Round Pushbutton
  S3 = Round Pushbutton
  J1 = Basic Servo

nets:
  N1: Composant1.ICSP_MISO, Composant1.D12/MISO, Arduino_CNC_Shield_V3_00_1.SpnEn_/_Z_Limit
  N2: Composant1.5V, Arduino_CNC_Shield_V3_00_1.SpnEn_(Gnd), S2.leg0
  N3: Composant1.ICSP_SCK, Arduino_CNC_Shield_V3_00_1.SpnDir
  N4: Composant1.ICSP_MOSI, Arduino_CNC_Shield_V3_00_1.SpnDir_(Gnd)
  N5: Composant1.RESET, Arduino_CNC_Shield_V3_00_1.CoolEn
  N6: Composant1.GND, Arduino_CNC_Shield_V3_00_1.CoolEn_(Gnd), S2.leg1, S3.leg1
  GND: M1.gnd, M2.gnd, M3.Pin_4, ESP32_-_Back2.GND, ESP32_-_Back3.GND, M7.gnd, M8.gnd, J1.gnd
  VCC: M1.vcc, M2.vcc, M3.Pin_3, ESP32_-_Back2.5V, M8.vcc
  N7: M1.pulse, ESP32_-_Back3.GPIO14
  N8: M2.pulse, ESP32_-_Back3.GPIO15
  N9: M3.Pin_1, Power_plug2.VCC
  N10: M3.Pin_2, Power_plug2.GND
  N11: ESP32_-_Back3.GPIO2, M8.pulse
  N12: ESP32_-_Back3.GPIO13, M7.pulse
  N13: ESP32_-_Back3.GPIO12, J1.pulse
  VCC_2: ESP32_-_Back3.5V, M7.vcc, J1.vcc
  N14: M4.A, Arduino_CNC_Shield_V3_00_1.Y-MTR_'4'
  N15: M4.C, Arduino_CNC_Shield_V3_00_1.Y-MTR_'3'
  N16: M4.B, Arduino_CNC_Shield_V3_00_1.Y-MTR_'2'
  N17: M4.D, Arduino_CNC_Shield_V3_00_1.Y-MTR_'1'
  N18: M5.A, Arduino_CNC_Shield_V3_00_1.Z-MTR_'4'
  N19: M5.C, Arduino_CNC_Shield_V3_00_1.Z-MTR_'3'
  N20: M5.B, Arduino_CNC_Shield_V3_00_1.Z-MTR_'2'
  N21: M5.D, Arduino_CNC_Shield_V3_00_1.Z-MTR_'1'
  N22: M6.A, Arduino_CNC_Shield_V3_00_1.X-MTR_'4'
  N23: M6.C, Arduino_CNC_Shield_V3_00_1.X-MTR_'3'
  N24: M6.B, Arduino_CNC_Shield_V3_00_1.X-MTR_'2'
  N25: M6.D, Arduino_CNC_Shield_V3_00_1.X-MTR_'1'
  N26: Arduino_CNC_Shield_V3_00_1.POWER_-, Power_plug1.GND
  N27: Arduino_CNC_Shield_V3_00_1.POWER_+, Power_plug1.VCC

custom parts:
  ESP32 - CAM: The ESP32-CAM has a very competitive small-size camera module that can operate independently as a minimum system with a footprint of only 27*40.5*4.5mm and a deep sleep current of up to 6mA.
  Arduino_CNC_V3.00: Protoneer Arduino CNC Shield V3.00 If using Grbl V0.9: The “A” axis can not be used (yet). The “SCL” (Arduino A5) pin is now used for 'Probing' input. The “End Stops Z+ & Z-” (Arduino D11) and “SpnEn” (Arduino D12) have been switched!
