# Fritzing sketch electronic_sketch_with_WeMos (saved by Fritzing 1.0.4)

parts:
  Composant1 = Arduino Uno (Rev3) - ICSP
  LCD1 = LCD screen  # not connected
  IC1 = SELECTOR_MULTIPLEXER [package=so016]  # not connected
  M3 = RioRand LM2596
  Composant2 = InvenSense MPU6050  # not connected
  ESP32_-_Back2 = ESP32 - CAM  # not connected
  M4 = Stepper Motor - Bipolar
  M5 = Stepper Motor - Bipolar
  M6 = Stepper Motor - Bipolar
  RE1 = Rotary Encoder [package=THT]  # not connected
  Arduino_CNC_Shield_V3_00_1 = Arduino_CNC_V3.00
  Power_plug2 = Power plug
  M9 = >Wemos D1 R32
  JL012-13-5_1 = JL012-13-5.2 Lever (Limit) Switch SPDT + NO + NC [part_number=JL012-13-5.2]
  JL012-13-5_2 = JL012-13-5.2 Lever (Limit) Switch SPDT + NO + NC [part_number=JL012-13-5.2]
  Composant3 = Adafruit PCA9685 PWM/Servo Breakout [part_number=815]
  J1 = Basic Servo
  M10 = Dagu DGServo 9g (Top view) [part_number=RS001B]
  M11 = Dagu DGServo 9g (Top view) [part_number=RS001B]
  M12 = Dagu DGServo 9g (Top view) [part_number=RS001B]
  M13 = Dagu DGServo 9g (Top view) [part_number=RS001B]

nets:
  GND: Composant1.GND, M9.GND, JL012-13-5_1.C, Composant3.GND, J1.gnd, M10.gnd, M11.gnd, M12.gnd, M13.gnd
  N1: Composant1.D4, JL012-13-5_1.NO
  N2: Composant1.D6_PWM, M9.IO26
  N3: Composant1.D7, JL012-13-5_2.NO
  N4: M3.Pin_1, Power_plug2.VCC
  N5: M3.Pin_2, Power_plug2.GND
  N6: M3.Pin_3, Arduino_CNC_Shield_V3_00_1.POWER_+
  N7: M3.Pin_4, Arduino_CNC_Shield_V3_00_1.POWER_-
  N8: M4.A, Arduino_CNC_Shield_V3_00_1.Y-MTR_'4'
  N9: M4.C, Arduino_CNC_Shield_V3_00_1.Y-MTR_'3'
  N10: M4.B, Arduino_CNC_Shield_V3_00_1.Y-MTR_'2'
  N11: M4.D, Arduino_CNC_Shield_V3_00_1.Y-MTR_'1'
  N12: M5.A, Arduino_CNC_Shield_V3_00_1.Z-MTR_'4'
  N13: M5.C, Arduino_CNC_Shield_V3_00_1.Z-MTR_'3'
  N14: M5.B, Arduino_CNC_Shield_V3_00_1.Z-MTR_'2'
  N15: M5.D, Arduino_CNC_Shield_V3_00_1.Z-MTR_'1'
  N16: M6.A, Arduino_CNC_Shield_V3_00_1.X-MTR_'4'
  N17: M6.C, Arduino_CNC_Shield_V3_00_1.X-MTR_'3'
  N18: M6.B, Arduino_CNC_Shield_V3_00_1.X-MTR_'2'
  N19: M6.D, Arduino_CNC_Shield_V3_00_1.X-MTR_'1'
  5V: M9.5V, Composant3.VCC
  N20: M9.SDA, Composant3.SDA
  N21: M9.SCL, Composant3.SCL
  N22: Composant3.PWM4, M13.pulse
  VCC: Composant3.5.0V, J1.vcc, M10.vcc, M11.vcc, M12.vcc, M13.vcc
  N23: Composant3.PWM3, M11.pulse
  N24: Composant3.PWM2, M10.pulse
  N25: Composant3.PWM1, M12.pulse
  N26: Composant3.PWM0, J1.pulse

custom parts:
  ESP32 - CAM: The ESP32-CAM has a very competitive small-size camera module that can operate independently as a minimum system with a footprint of only 27*40.5*4.5mm and a deep sleep current of up to 6mA.
  Arduino_CNC_V3.00: Protoneer Arduino CNC Shield V3.00 If using Grbl V0.9: The “A” axis can not be used (yet). The “SCL” (Arduino A5) pin is now used for 'Probing' input. The “End Stops Z+ & Z-” (Arduino D11) and “SpnEn” (Arduino D12) have been switched!
  >Wemos D1 R32: Wemos D1 R32 - This board is used with dual-mode Wi-Fi and Bluetooth chips, which is safe, reliable, and scalable to a variety of applications. DC in 5V-12V, 1 analog input(3.2V max input), a Micro USB connection, Compatible with D1 R32=WiFi+bluetooth+UNO
  JL012-13-5.2 Lever (Limit) Switch SPDT + NO + NC: Micro Switch; Model No.: JL012-13.5-2; Actuator Action: Momentary; Actuator Type: Hinge Lever; Contact Configuration: 1NO, 1NC (SPDT) Temperature -25~65℃；Relative humidity: below 85%; Rate Voltage: 125V AC; Rated Current: 1A.
  Adafruit PCA9685 PWM/Servo Breakout: Using only two pins, control 16 free-running PWM outputs! I2C-controlled PWM driver with a built in clock. Unlike the TLC5940 family, you do not need to continuously send it signal tying up your microcontroller, its completely free running! 5V compliant, which means you can control it from a 3.3V microcontroller and still safely drive up to 6V outputs (this is good for when you want to control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
